# Fritzing sketch Caparacho (saved by Fritzing 0.9.3b)

parts:
  Componente1 = Arduino Uno (Rev3)
  J1 = RJ11 Jack [package=rj11-6]
  J2 = RJ11 Jack [package=rj11-6]
  J3 = RJ11 Jack [package=rj11-6]
  J4 = RJ11 Jack [package=rj11-6]
  J5 = RJ11 Jack [package=rj11-6]
  J6 = RJ11 Jack [package=rj11-6]
  J7 = RJ11 Jack [package=rj11-6]
  J8 = RJ11 Jack [package=rj11-6]
  J9 = RJ11 Jack [package=rj11-6]
  S2 = Pushbutton [package="[SMD]"]
  U1 = SWITCH-SPST-2 [package=switch-spst-vertical]
  VCC1 = 4 x AAA Battery Mount
  VCC2 = 4 x AAA Battery Mount
  R1 = Resistor [tolerance=±5% resistance=1.5k package=THT]
  LED1 = LED - 5mm [color="Yellow (595nm)" package="5 mm [THT]"]

nets:
  N1: Componente1.A0, J4.4
  N2: Componente1.A1, J4.5
  N3: Componente1.A2, J5.4
  N4: Componente1.A3, J5.5
  N5: Componente1.A4/SDA, J6.4
  N6: Componente1.A5/SCL, J6.5
  N7: Componente1.D8, J2.5
  N8: Componente1.D9_PWM, J8.5
  N9: Componente1.D10_PWM/SS, J9.4
  N10: Componente1.D11_PWM/MOSI, J9.5
  N11: Componente1.D12/MISO, J3.4
  N12: Componente1.D13/SCK, J3.5
  N13: Componente1.GND, J1.2, J2.2, J3.2, J4.2, J5.2, J6.2, J7.2, J8.2, J9.2, S2.Pin_3, S2.Pin_4, VCC1.-
  N14: Componente1.D2, J1.4
  N15: Componente1.D3_PWM, J7.4
  N16: Componente1.D4, J1.5
  N17: Componente1.D5_PWM, J7.5
  N18: Componente1.D6_PWM, J8.4
  N19: Componente1.D7, J2.4
  N20: Componente1.RESET, S2.Pin_2
  N21: Componente1.VIN, J1.3, J2.3, J3.3, J4.3, J5.3, J6.3, J7.3, J8.3, J9.3, U1.O
  N22: U1.P, LED1.cathode
  N23: VCC1.+, VCC2.-
  N24: VCC2.+, R1.Pin_1
  N25: R1.Pin_0, LED1.anode

notes:
  1.5kΩ
  X1
  d2 y d4
  X2
  d7 y d8
  X3
  d12 y d13
  Y1
  p3 y p5
  Y2
  p6 y p9
  Y3
  p10 y p11
  Z1
  a0 y a1
  Z2
  a2 y a3
  reset
  y GND
  Z3
  a4 y a5
  12V
