# Fritzing sketch controlador_de_dos_motores_sin_enable (saved by Fritzing 0.9.3b)
circuit board: 4.4261cm x 3.35153cm

parts:
  M1 = DC Motor
  M2 = DC Motor
  IC1 = L293D [package=THT]
  J1 = RJ11 Jack [package=rj11-6]
  J2 = RJ11 Jack [package=rj11-6]

nets:
  N1: M1.pin_1, IC1.Out_4_(_Controlled_by_Enable_2_)
  N2: M1.pin_2, IC1.Out_3_(_Controlled_by_Enable_2_)
  N3: M2.pin_1, IC1.Out_1_(_Controlled_by_Enable_1_)
  N4: M2.pin_2, IC1.Out_2_(_Controlled_by_Enable_1_)
  N5: IC1.In_1, J2.4
  N6: IC1.0V, J1.2, J2.2
  N7: IC1.In_2, J2.5
  N8: IC1.+Vmotor, J2.3
  N9: IC1.In_3, J1.4
  N10: IC1.In_4, J1.5
  N11: IC1.+V, J1.3
